# Fritzing sketch part1-single-led-5v (saved by Fritzing 0.9.2b)
breadboards: 1

parts:
  Raspberry_Pi1 = Raspberry Pi B rev2
  LED1 = LED - 5mm [color="Red (633nm)" package="5 mm [THT]"]
  R1 = Resistor [tolerance=±5% resistance=220 package=THT]

nets:
  N1: Raspberry_Pi1.5V, LED1.anode
  N2: Raspberry_Pi1.GND, R1.Pin_1
  N3: LED1.cathode, R1.Pin_0
