# Fritzing sketch part3-all-three-leds (saved by Fritzing 0.9.2b)
breadboards: 1

parts:
  Raspberry_Pi1 = Raspberry Pi B rev2
  LED1 = LED - 5mm [color="Red (633nm)" package="5 mm [THT]"]
  R1 = Resistor [tolerance=±5% resistance=220 package=THT]
  LED2 = LED - 5mm [color="Yellow (592nm)" package="5 mm [THT]"]
  R2 = Resistor [tolerance=±5% resistance=220 package=THT]
  LED3 = LED - 5mm [color="Green (565nm)" package="5 mm [THT]"]
  R3 = Resistor [tolerance=±5% resistance=220 package=THT]

nets:
  N1: Raspberry_Pi1.GND, Raspberry_Pi1.GPIO_25, R1.Pin_1, R2.Pin_1, LED3.anode, R3.Pin_1
  N2: Raspberry_Pi1.GPIO_23, LED2.anode
  N3: Raspberry_Pi1.GPIO_18, LED1.anode
  N4: LED1.cathode, R1.Pin_0
  N5: LED2.cathode, R2.Pin_0
  N6: LED3.cathode, R3.Pin_0
