# Fritzing sketch part3-button-gpio4 (saved by Fritzing 0.9.2b)
breadboards: 1

parts:
  Raspberry_Pi3 = Raspberry Pi 2
  LED3 = LED - 5mm [color="Red (635nm)" package="5 mm [THT]"]
  R3 = Resistor [tolerance=±5% resistance=220 package=THT]
  S1 = Pushbutton [package="[THT]"]
  R4 = Resistor [tolerance=±5% resistance=10k package=THT]

nets:
  N1: Raspberry_Pi3.GPIO4, LED3.anode
  N2: Raspberry_Pi3.3V3, S1.Pin_3, S1.Pin_4
  N3: Raspberry_Pi3.GPIO5, S1.Pin_1, S1.Pin_2, R4.Pin_0
  N4: Raspberry_Pi3.GND, R3.Pin_1, R4.Pin_1
  N5: LED3.cathode, R3.Pin_0
